// Logisim project ch17.circ as structural Verilog: 13 circuits, main circuit main
module main (
  input  R,
  input  Clock,
  input  S,
  output Q,
  output Qbar
);

  wire and_1_out, and_2_out;

  S_R_Flip_Flop s_r_ff_1 ();  // open: S, R, clk, Q, reset, Qn, preset
  and and_1 (and_1_out, R, Clock);
  and and_2 (and_2_out, Clock, S);
  nor nor_1 (Q, and_1_out, Qbar);
  nor nor_2 (Qbar, Q, and_2_out);

  // Notes on the sheet:
  //   Asynchronous Set
  //   Asynchronous reset
endmodule

module fadder (
  input  a,
  input  b,
  input  c,
  output Sum,
  output Carry
);

  wire AB_out, AC_out, BC_out;

  xor xor_1 (Sum, a, b, c);
  and AB (AB_out, a, b);
  and AC (AC_out, c, a);
  and BC (BC_out, b, c);
  or or_1 (Carry, AB_out, AC_out, BC_out);
endmodule

module fourbitadder (
  input  A0,
  input  B0,
  input  C,
  input  A1,
  input  B1,
  input  A2,
  input  B2,
  input  A3,
  input  B3,
  output s0,
  output s1,
  output s2,
  output s3,
  output Cout
);

  wire adder0_carry, adder1_carry, adder2_carry;

  fadder adder0 (.a(A0), .b(B0), .c(C), .Sum(s0), .Carry(adder0_carry));
  fadder adder1 (.a(A1), .b(B1), .c(adder0_carry), .Sum(s1), .Carry(adder1_carry));
  fadder adder2 (.a(A2), .b(B2), .c(adder1_carry), .Sum(s2), .Carry(adder2_carry));
  fadder adder3 (.a(A3), .b(B3), .c(adder2_carry), .Sum(s3), .Carry(Cout));
endmodule

module eightbitadder (
  input  a0,
  input  b0,
  input  c,
  input  a1,
  input  b1,
  input  a2,
  input  b2,
  input  a3,
  input  b3,
  input  a4,
  input  b4,
  input  a5,
  input  b5,
  input  a6,
  input  b6,
  input  a7,
  input  b7,
  output s0,
  output s1,
  output s2,
  output s3,
  output s4,
  output s5,
  output s6,
  output s7,
  output Cout
);

  wire fourbitadder_1_cout;

  fourbitadder fourbitadder_1 (
    .A0(a0), .B0(b0), .C(c), .A1(a1), .B1(b1), .A2(a2), .B2(b2), .A3(a3), .B3(b3), .s0(s0), .s1(s1), .s2(s2),
    .s3(s3), .Cout(fourbitadder_1_cout));
  fourbitadder fourbitadder_2 (
    .A0(a4), .B0(b4), .C(fourbitadder_1_cout), .A1(a5), .B1(b5), .A2(a6), .B2(b6), .A3(a7), .B3(b7), .s0(s4),
    .s1(s5), .s2(s6), .s3(s7), .Cout(Cout));
endmodule

module sixteenbitadder (
);

  eightbitadder eightbitadder_1 ();  // open: a0, b0, c, a1, b1, a2, b2, a3, b3, a4, b4, a5, b5, a6, b6, a7, b7, s0, s1, s2, s3, s4, s5, s6, s7, Cout
  eightbitadder eightbitadder_2 ();  // open: a0, b0, c, a1, b1, a2, b2, a3, b3, a4, b4, a5, b5, a6, b6, a7, b7, s0, s1, s2, s3, s4, s5, s6, s7, Cout
endmodule

module signed_adder (
  input  cin,
  input  a,
  input  b,
  input  b_inv,
  output S,
  output C
);

  wire multiplexer_1_out, not_1_out;

  not not_1 (not_1_out, b);
  Multiplexer multiplexer_1 (.in0(b), .in1(not_1_out), .out(multiplexer_1_out), .sel(b_inv));
  fadder fadder_1 (.a(a), .b(multiplexer_1_out), .c(cin), .Sum(S), .Carry(C));
endmodule

module signed4_adder (
  input  binv,
  input  cin,
  input  a0,
  input  b0,
  input  a1,
  input  b1,
  input  a2,
  input  b2,
  input  a3,
  input  b3,
  output s0,
  output s1,
  output s2,
  output s3,
  output cout
);

  wire signed_adder_1_c, signed_adder_2_c, signed_adder_3_c;

  signed_adder signed_adder_1 (.cin(cin), .b_inv(binv), .S(s0), .C(signed_adder_1_c));  // open: a, b
  signed_adder signed_adder_2 (.cin(signed_adder_1_c), .a(a1), .b(b1), .b_inv(binv), .S(s1), .C(signed_adder_2_c));
  signed_adder signed_adder_3 (.cin(signed_adder_2_c), .a(a2), .b(b2), .b_inv(binv), .S(s2), .C(signed_adder_3_c));
  signed_adder signed_adder_4 (.cin(signed_adder_3_c), .a(a3), .b(b3), .b_inv(binv), .S(s3), .C(cout));
endmodule

module RS_flip_flop (
  input  R,
  input  S,
  input  Reset,
  input  Clk,
  input  Set,
  input  in_6,
  input  in_7,
  input  in_8,
  input  in_9,
  input  clock,
  input  enable,
  input  clear,
  output Q,
  output Qbar,
  output Q1,
  output Q1bar,
  output out_17,
  output out_18
);

  wire and_1_out, and_2_out;

  S_R_Flip_Flop s_r_ff_1 (.S(in_7), .R(in_8), .clk(clock), .Q(out_17), .reset(in_9), .Qn(out_18), .preset(in_6));
  and and_1 (and_1_out, Reset, Clk);
  and and_2 (and_2_out, Clk, Set);
  nor nor_1 (Q, R, Qbar);
  nor nor_2 (Qbar, Q, S);
  // Digital_Oscilloscope digital_oscilloscope_1: pin names not known; wires that end beside it: clock, in_8, in_7, out_17, enable, clear
  nor nor_3 (Q1, and_1_out, Q1bar);
  nor nor_4 (Q1bar, Q1, and_2_out);

  // Notes on the sheet:
  //   RS Flip flop with a clk
  //   R S Flip flop
endmodule

module delatch (
  input  data,
  input  Clk,
  output Q1,
  output Q1bar
);

  wire and_1_out, and_2_out;

  and and_1 (and_1_out, ~data, Clk);  // AND_Gate
  and and_2 (and_2_out, Clk, data);
  nor nor_1 (Q1, and_1_out, Q1bar);
  nor nor_2 (Q1bar, Q1, and_2_out);

  // Notes on the sheet:
  //   Level Triggered D latch
endmodule

module d_latch_edge_trigger (
  input  data,
  input  clk,
  input  enable,
  input  clear,
  output Q
);

  wire delatch_1_q1, not_1_out;

  not not_1 (not_1_out, clk);
  delatch delatch_1 (.data(data), .Clk(not_1_out), .Q1(delatch_1_q1));  // open: Q1bar
  // Digital_Oscilloscope digital_oscilloscope_1: pin names not known; wires that end beside it: clk, data, Q, enable, clear
  delatch delatch_2 (.data(delatch_1_q1), .Clk(clk), .Q1(Q));  // open: Q1bar
endmodule

module fourbit_register (
  input  d3,
  input  d2,
  input  d1,
  input  \do ,
  input  set,
  input  clk,
  input  reset,
  output q3,
  output q2,
  output q1,
  output q0
);

  D_Flip_Flop d_ff_1 (.D(d3), .clk(clk), .Q(q3), .preset(set), .reset(reset));  // open: Qn
  D_Flip_Flop d_ff_2 (.D(d2), .clk(clk), .Q(q2), .preset(set), .reset(reset));  // open: Qn
  Hex_Digit_Display hex_digit_display_1 (.value({q3, q2, q1, q0}));  // open: dp
  D_Flip_Flop d_ff_3 (.D(d1), .clk(clk), .Q(q1), .preset(set), .reset(reset));  // open: Qn
  D_Flip_Flop d_ff_4 (.D(\do ), .clk(clk), .Q(q0), .preset(set), .reset(reset));  // open: Qn
endmodule

module fourBit_accumulator (
  input  subtract,
  input  b3,
  input  b2,
  input  b1,
  input  b0,
  input  set,
  input  reset
);

  wire button_1_out, signed4_adder_1_s0, signed4_adder_1_s1, signed4_adder_1_s2, signed4_adder_1_s3;
  wire [3:0] fourbit_register_1_q0;

  signed4_adder signed4_adder_1 (
    .binv(subtract), .cin(subtract), .a0(fourbit_register_1_q0[0]), .b0(b0), .a1(fourbit_register_1_q0[1]),
    .b1(b1), .a2(fourbit_register_1_q0[2]), .b2(b2), .a3(fourbit_register_1_q0[3]), .b3(b3),
    .s0(signed4_adder_1_s0), .s1(signed4_adder_1_s1), .s2(signed4_adder_1_s2), .s3(signed4_adder_1_s3));  // open: cout
  Button button_1 (.out(button_1_out));
  fourbit_register fourbit_register_1 (
    .d3(signed4_adder_1_s3), .d2(signed4_adder_1_s2), .d1(signed4_adder_1_s1), .\do (signed4_adder_1_s0),
    .set(set), .clk(button_1_out), .reset(reset), .q3(fourbit_register_1_q0[3]),
    .q2(fourbit_register_1_q0[2]), .q1(fourbit_register_1_q0[1]), .q0(fourbit_register_1_q0[0]));
  LED led_1 (.in(fourbit_register_1_q0[3]));
  LED led_2 (.in(fourbit_register_1_q0[2]));
  Hex_Digit_Display hex_digit_display_1 (.value(fourbit_register_1_q0));  // open: dp
  LED led_3 (.in(fourbit_register_1_q0[1]));
  LED led_4 (.in(fourbit_register_1_q0[0]));
endmodule

module freq_divider (
  input  enable,
  input  clear
);

  wire clock_1_out, d_ff_1_q, d_ff_1_qn;

  Clock clock_1 (.out(clock_1_out));
  D_Flip_Flop d_ff_1 (.D(d_ff_1_qn), .clk(clock_1_out), .Q(d_ff_1_q), .Qn(d_ff_1_qn));  // open: preset, reset
  // Digital_Oscilloscope digital_oscilloscope_1: pin names not known; wires that end beside it: clock_1_out, d_ff_1_q, enable, clear
endmodule
