// Logisim project Clocks.circ as structural Verilog: 1 circuit, main circuit main
module main (
);

  wire and_1_out, and_2_out, and_3_out, and_4_out, and_5_out, and_6_out, b0000_out, b0001_out, b0010_out,
       b0011_out, b0100_out, b0101_out, b0110_out, b0111_out, b1000_out, clock_1_out, d_ff_1_q, d_ff_1_qn,
       d_ff_2_q, d_ff_2_qn, d_ff_3_q, d_ff_3_qn, d_ff_4_q, d_ff_4_qn, d_ff_5_q, d_ff_5_qn, d_ff_6_q,
       d_ff_6_qn, d_ff_7_q, d_ff_7_qn, d_ff_8_q, d_ff_8_qn, d_ff_9_q, d_ff_9_qn, d_ff_10_q, d_ff_10_qn,
       d_ff_11_q, d_ff_11_qn, d_ff_12_q, d_ff_12_qn, d_ff_13_q, d_ff_13_qn, d_ff_14_q, d_ff_14_qn, d_ff_15_q,
       d_ff_15_qn, d_ff_16_q, d_ff_16_qn, d_ff_17_q, d_ff_17_qn, d_ff_18_q, d_ff_18_qn, d_ff_19_q,
       d_ff_19_qn, N0_out, N1_out, N2_out, N3_out, N4_out, N5_out, N_0_out, N_1_out, N_2_out, N_3_out,
       N_4_out, N_5_out, N_6_out, N_7_out, N_8_out, nand_2_out, nand_3_out, nand_4_out, nand_5_out,
       nand_6_out, nor_1_out, nor_2_out, nor_3_out, nor_4_out, nor_5_out, nor_6_out, nor_7_out, nor_8_out,
       nor_9_out, nor_10_out, nor_11_out, nor_12_out, nor_13_out, nor_14_out, nor_15_out, nor_16_out,
       nor_17_out, nor_18_out, nor_19_out, nor_20_out, nor_21_out, nor_22_out, nor_23_out, nor_24_out,
       nor_25_out, nor_26_out, not_1_out, not_2_out, not_3_out, not_4_out, not_5_out, not_6_out, not_7_out,
       not_8_out, not_9_out, not_10_out, not_11_out, not_12_out, not_13_out, not_14_out, not_15_out,
       not_16_out, not_17_out, not_18_out, not_19_out, not_20_out, not_21_out, not_22_out, not_23_out,
       not_24_out, Num_0_out, Num_1_out, Num_2_out, Num_3_out, Num_4_out, Num_5_out, or_1_out, or_2_out,
       or_3_out, or_4_out, or_5_out, or_6_out, or_7_out, or_8_out, or_9_out, x0_out, x1_out, x2_out, x3_out,
       x4_out, x5_out, x6_out, x7_out, x8_out;

  not not_1 (not_1_out, or_1_out);
  or or_1 (or_1_out, d_ff_5_q, nor_1_out);
  _7_Segment_Display u_7_segment_display_1 (
    .g(not_1_out), .f(not_1_out), .a(not_1_out), .b(or_2_out), .e(not_1_out), .d(not_1_out), .c(or_2_out));  // open: dp
  or or_2 (or_2_out, or_1_out, not_1_out);
  not not_2 (not_2_out, d_ff_1_q);
  nor nor_1 (nor_1_out, d_ff_5_q, d_ff_4_q, d_ff_3_q, d_ff_2_q, d_ff_1_q);
  D_Flip_Flop d_ff_1 (.D(d_ff_1_qn), .clk(nand_3_out), .Q(d_ff_1_q), .Qn(d_ff_1_qn), .reset(or_5_out));  // open: preset
  not not_3 (not_3_out, or_3_out);
  D_Flip_Flop d_ff_2 (.D(d_ff_2_qn), .clk(d_ff_1_qn), .Q(d_ff_2_q), .Qn(d_ff_2_qn), .reset(or_5_out));  // open: preset
  nor nor_2 (nor_2_out, N_1_out, N_4_out);
  and N_0 (N_0_out, not_6_out, not_4_out, not_3_out, not_2_out);
  or or_3 (or_3_out, nor_1_out, d_ff_2_q);
  D_Flip_Flop d_ff_3 (.D(d_ff_3_qn), .clk(d_ff_2_qn), .Q(d_ff_3_q), .Qn(d_ff_3_qn), .reset(or_5_out));  // open: preset
  nor nor_3 (nor_3_out, N_1_out, N_2_out, N_3_out, N_7_out);
  and N_1 (N_1_out, not_6_out, not_4_out, not_3_out, d_ff_1_q);
  and N_2 (N_2_out, not_6_out, not_4_out, or_3_out, not_2_out);
  _7_Segment_Display u_7_segment_display_2 (
    .g(nor_5_out), .f(nor_3_out), .a(nor_2_out), .b(nor_6_out), .e(or_4_out), .d(nor_4_out), .c(not_5_out));  // open: dp
  or or_4 (or_4_out, N_0_out, N_2_out, N_6_out, N_8_out);
  and N_3 (N_3_out, not_6_out, not_4_out, or_3_out, d_ff_1_q);
  D_Flip_Flop d_ff_4 (.D(d_ff_4_qn), .clk(d_ff_3_qn), .Q(d_ff_4_q), .Qn(d_ff_4_qn), .reset(or_5_out));  // open: preset
  nor nor_4 (nor_4_out, N_1_out, N_4_out, N_7_out);
  and N_4 (N_4_out, not_6_out, d_ff_3_q, not_3_out, not_2_out);
  not not_4 (not_4_out, d_ff_3_q);
  // NAND_Gate nand_1 has open pins: in0=d_ff_5_q, in1=d_ff_1_q, out=open
  and and_1 (and_1_out, d_ff_2_q, ~d_ff_4_q, d_ff_5_q);  // AND_Gate
  and and_2 (and_2_out, d_ff_2_qn, d_ff_4_q);
  nand nand_2 (nand_2_out, d_ff_1_q, d_ff_4_q);
  or or_5 (or_5_out, and_1_out, and_2_out);
  not not_5 (not_5_out, N_2_out);
  and N_5 (N_5_out, not_6_out, d_ff_3_q, not_3_out, d_ff_1_q);
  not not_6 (not_6_out, d_ff_4_q);
  D_Flip_Flop d_ff_5 (
    .D(d_ff_5_qn), .clk(nand_2_out), .Q(d_ff_5_q), .Qn(d_ff_5_qn), .reset(and_2_out));  // open: preset
  nor nor_5 (nor_5_out, N_0_out, N_1_out, N_7_out);
  and N_6 (N_6_out, not_6_out, d_ff_3_q, or_3_out, not_2_out);
  nor nor_6 (nor_6_out, N_5_out, N_6_out);
  and N_7 (N_7_out, not_6_out, d_ff_3_q, or_3_out, d_ff_1_q);
  and N_8 (N_8_out, d_ff_4_q, not_4_out, not_3_out, not_2_out);
  nor nor_7 (nor_7_out, Num_1_out, Num_4_out);
  and Num_0 (Num_0_out, not_7_out, not_8_out, not_9_out);
  not not_7 (not_7_out, d_ff_6_q);
  D_Flip_Flop d_ff_6 (
    .D(d_ff_6_qn), .clk(nand_4_out), .Q(d_ff_6_q), .Qn(d_ff_6_qn), .reset(and_3_out));  // open: preset
  nor nor_8 (nor_8_out, Num_1_out, Num_2_out, Num_3_out);
  and Num_1 (Num_1_out, d_ff_6_q, not_9_out, not_8_out);
  not not_8 (not_8_out, d_ff_7_q);
  _7_Segment_Display u_7_segment_display_3 (
    .g(nor_10_out), .f(nor_8_out), .a(nor_7_out), .b(nor_11_out), .e(or_6_out), .d(nor_9_out), .c(not_10_out));  // open: dp
  or or_6 (or_6_out, Num_0_out, Num_2_out);
  and Num_2 (Num_2_out, not_7_out, d_ff_7_q, not_9_out);
  D_Flip_Flop d_ff_7 (.D(d_ff_7_qn), .clk(d_ff_6_qn), .Q(d_ff_7_q), .Qn(d_ff_7_qn), .reset(and_3_out));  // open: preset
  nor nor_9 (nor_9_out, Num_1_out, Num_4_out);
  and Num_3 (Num_3_out, d_ff_6_q, d_ff_7_q, not_9_out);
  not not_9 (not_9_out, d_ff_8_q);
  not not_10 (not_10_out, Num_2_out);
  and Num_4 (Num_4_out, d_ff_8_q, not_8_out, not_7_out);
  D_Flip_Flop d_ff_8 (.D(d_ff_8_qn), .clk(d_ff_7_qn), .Q(d_ff_8_q), .Qn(d_ff_8_qn), .reset(and_3_out));  // open: preset
  nor nor_10 (nor_10_out, Num_0_out, Num_1_out);
  and Num_5 (Num_5_out, d_ff_8_q, not_8_out, d_ff_6_q);
  nand nand_3 (nand_3_out, d_ff_8_q, d_ff_6_q);
  and and_3 (and_3_out, d_ff_8_q, d_ff_7_q);
  not nor_11 (nor_11_out, Num_5_out);  // NOR_Gate
  D_Flip_Flop d_ff_9 (
    .D(d_ff_9_qn), .clk(nand_5_out), .Q(d_ff_9_q), .Qn(d_ff_9_qn), .reset(and_4_out));  // open: preset
  not not_11 (not_11_out, d_ff_9_q);
  nor nor_12 (nor_12_out, x1_out, x4_out);
  and x0 (x0_out, not_15_out, not_13_out, not_12_out, not_11_out);
  not not_12 (not_12_out, d_ff_10_q);
  D_Flip_Flop d_ff_10 (
    .D(d_ff_10_qn), .clk(d_ff_9_qn), .Q(d_ff_10_q), .Qn(d_ff_10_qn), .reset(and_4_out));  // open: preset
  nor nor_13 (nor_13_out, x1_out, x2_out, x3_out, x7_out);
  and x1 (x1_out, not_15_out, not_13_out, not_12_out, d_ff_9_q);
  D_Flip_Flop d_ff_11 (
    .D(d_ff_11_qn), .clk(d_ff_10_qn), .Q(d_ff_11_q), .Qn(d_ff_11_qn), .reset(and_4_out));  // open: preset
  or or_7 (or_7_out, x0_out, x2_out, x6_out, x8_out);
  and x2 (x2_out, not_15_out, not_13_out, d_ff_10_q, not_11_out);
  _7_Segment_Display u_7_segment_display_4 (
    .g(nor_15_out), .f(nor_13_out), .a(nor_12_out), .b(nor_16_out), .e(or_7_out), .d(nor_14_out),
    .c(not_14_out));  // open: dp
  nor nor_14 (nor_14_out, x1_out, x4_out, x7_out);
  and x3 (x3_out, not_15_out, not_13_out, d_ff_10_q, d_ff_9_q);
  not not_13 (not_13_out, d_ff_11_q);
  D_Flip_Flop d_ff_12 (
    .D(d_ff_12_qn), .clk(d_ff_11_qn), .Q(d_ff_12_q), .Qn(d_ff_12_qn), .reset(and_4_out));  // open: preset
  not not_14 (not_14_out, x2_out);
  and x4 (x4_out, not_15_out, d_ff_11_q, not_12_out, not_11_out);
  and x5 (x5_out, not_15_out, d_ff_11_q, not_12_out, d_ff_9_q);
  and x6 (x6_out, not_15_out, d_ff_11_q, d_ff_10_q, not_11_out);
  not not_15 (not_15_out, d_ff_12_q);
  nand nand_4 (nand_4_out, d_ff_9_q, d_ff_10_q);
  and and_4 (and_4_out, d_ff_10_q, d_ff_12_q);
  nor nor_15 (nor_15_out, x0_out, x1_out, x7_out);
  and x7 (x7_out, not_15_out, d_ff_11_q, d_ff_10_q, d_ff_9_q);
  nor nor_16 (nor_16_out, x5_out, x6_out);
  and x8 (x8_out, d_ff_12_q, not_13_out, not_12_out, not_11_out);
  D_Flip_Flop d_ff_13 (
    .D(d_ff_13_qn), .clk(nand_6_out), .Q(d_ff_13_q), .Qn(d_ff_13_qn), .reset(and_5_out));  // open: preset
  nor nor_17 (nor_17_out, N1_out, N4_out);
  and N0 (N0_out, not_16_out, not_17_out, not_18_out);
  not not_16 (not_16_out, d_ff_13_q);
  D_Flip_Flop d_ff_14 (
    .D(d_ff_14_qn), .clk(d_ff_13_qn), .Q(d_ff_14_q), .Qn(d_ff_14_qn), .reset(and_5_out));  // open: preset
  nor nor_18 (nor_18_out, N1_out, N2_out, N3_out);
  and N1 (N1_out, d_ff_13_q, not_18_out, not_17_out);
  or or_8 (or_8_out, N0_out, N2_out);
  and N2 (N2_out, not_16_out, d_ff_14_q, not_18_out);
  not not_17 (not_17_out, d_ff_14_q);
  D_Flip_Flop d_ff_15 (
    .D(d_ff_15_qn), .clk(d_ff_14_qn), .Q(d_ff_15_q), .Qn(d_ff_15_qn), .reset(and_5_out));  // open: preset
  _7_Segment_Display u_7_segment_display_5 (
    .g(nor_20_out), .f(nor_18_out), .a(nor_17_out), .b(nor_21_out), .e(or_8_out), .d(nor_19_out),
    .c(not_19_out));  // open: dp
  nor nor_19 (nor_19_out, N1_out, N4_out);
  and N3 (N3_out, d_ff_13_q, d_ff_14_q, not_18_out);
  not not_18 (not_18_out, d_ff_15_q);
  and and_5 (and_5_out, d_ff_15_q, d_ff_14_q);
  not not_19 (not_19_out, N2_out);
  and N4 (N4_out, d_ff_15_q, not_17_out, not_16_out);
  nand nand_5 (nand_5_out, d_ff_15_q, d_ff_13_q);
  nor nor_20 (nor_20_out, N0_out, N1_out);
  and N5 (N5_out, d_ff_15_q, not_17_out, d_ff_13_q);
  not nor_21 (nor_21_out, N5_out);  // NOR_Gate
  Clock clock_1 (.out(clock_1_out));
  D_Flip_Flop d_ff_16 (
    .D(d_ff_16_qn), .clk(clock_1_out), .Q(d_ff_16_q), .Qn(d_ff_16_qn), .reset(and_6_out));  // open: preset
  _7_Segment_Display u_7_segment_display_6 (
    .g(nor_25_out), .f(nor_23_out), .a(nor_22_out), .b(nor_26_out), .e(or_9_out), .d(nor_24_out),
    .c(not_23_out));  // open: dp
  D_Flip_Flop d_ff_17 (
    .D(d_ff_17_qn), .clk(d_ff_16_qn), .Q(d_ff_17_q), .Qn(d_ff_17_qn), .reset(and_6_out));  // open: preset
  D_Flip_Flop d_ff_18 (
    .D(d_ff_18_qn), .clk(d_ff_17_qn), .Q(d_ff_18_q), .Qn(d_ff_18_qn), .reset(and_6_out));  // open: preset
  not not_20 (not_20_out, d_ff_16_q);
  D_Flip_Flop d_ff_19 (
    .D(d_ff_19_qn), .clk(d_ff_18_qn), .Q(d_ff_19_q), .Qn(d_ff_19_qn), .reset(and_6_out));  // open: preset
  not not_21 (not_21_out, d_ff_17_q);
  nor nor_22 (nor_22_out, b0001_out, b0100_out);
  and b0000 (b0000_out, not_24_out, not_22_out, not_21_out, not_20_out);
  nor nor_23 (nor_23_out, b0001_out, b0010_out, b0011_out, b0111_out);
  and b0001 (b0001_out, not_24_out, not_22_out, not_21_out, d_ff_16_q);
  and b0010 (b0010_out, not_24_out, not_22_out, d_ff_17_q, not_20_out);
  nand nand_6 (nand_6_out, d_ff_16_q, d_ff_19_q);
  and and_6 (and_6_out, d_ff_17_q, d_ff_19_q);
  or or_9 (or_9_out, b0000_out, b0010_out, b0110_out, b1000_out);
  and b0011 (b0011_out, not_24_out, not_22_out, d_ff_17_q, d_ff_16_q);
  nor nor_24 (nor_24_out, b0001_out, b0100_out, b0111_out);
  and b0100 (b0100_out, not_24_out, d_ff_18_q, not_21_out, not_20_out);
  not not_22 (not_22_out, d_ff_18_q);
  not not_23 (not_23_out, b0010_out);
  and b0101 (b0101_out, not_24_out, d_ff_18_q, not_21_out, d_ff_16_q);
  not not_24 (not_24_out, d_ff_19_q);
  nor nor_25 (nor_25_out, b0000_out, b0001_out, b0111_out);
  and b0110 (b0110_out, not_24_out, d_ff_18_q, d_ff_17_q, not_20_out);
  and b0111 (b0111_out, not_24_out, d_ff_18_q, d_ff_17_q, d_ff_16_q);
  nor nor_26 (nor_26_out, b0101_out, b0110_out);
  and b1000 (b1000_out, d_ff_19_q, not_22_out, not_21_out, not_20_out);

  // Notes on the sheet:
  //   Tens of Hours
  //   Hours
  //   12 hour period
  //   Overflow bit
  //   4 to 9 decoder
  //   Tens of Minutes
  //   1 hour period
  //   3 to 6 decoder
  //   Minutes
  //   10 min period
  //   4 to 9 decoder
  //   Tens of secnds
  //   1 min period
  //   3 to 6 decoder
  //   Seconds
  //   0-9 seconds
  //   10 Second period
  //   4 to 9 decoder
endmodule
